# Fritzing sketch 3 OLED Clock (saved by Fritzing 0.9.3b)

parts:
  Part1 = Arduino Nano (Rev3.0)
  Part2 = Adafruit TCA9548A
  OLED_I2C1 = OLED 128x64 I2C Monochrome Display
  OLED_I2C2 = OLED 128x64 I2C Monochrome Display
  OLED_I2C3 = OLED 128x64 I2C Monochrome Display
  ZS-042_RTC1 = ZS-042 RTC Module
  S1 = Square Pushbutton
  R3 = Resistor [tolerance=±5% resistance=100 package=THT]

nets:
  N1: Part1.D2, S1.leg1
  GND: Part1.GND, Part2.GND
  5V: Part1.5V, Part2.VCC
  N2: Part1.A5, Part2.INPUTSCL
  N3: Part1.A4, Part2.INPUTSDA
  N4: Part2.2SDA, OLED_I2C1.SDA
  N5: Part2.2SCL, OLED_I2C1.SCK
  N6: Part2.3SDA, OLED_I2C2.SDA
  N7: Part2.3SCL, OLED_I2C2.SCK
  N8: Part2.4SDA, OLED_I2C3.SDA
  N9: Part2.4SCL, OLED_I2C3.SCK
  N10: ZS-042_RTC1.GND, R3.Pin_0
  N11: S1.leg0, R3.Pin_1

custom parts:
  Adafruit TCA9548A: You just found the perfect I2C sensor, and you want to wire up two or three or more of them to your Arduino when you realize "Uh oh, this chip has a fixed I2C address, and from what I know about I2C, you cannot have two devices with the same address on the same SDA/SCL pins!" Are you out of luck? You would be, if you didn't have this ultra-cool TCA9548A 1-to-8 I2C multiplexer! Finally, a way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
