# Fritzing sketch 3-Screen-OLED-Clock (saved by Fritzing 0.9.3b)

parts:
  Part1 = Arduino Nano (Rev3.0)
  Part2 = Adafruit TCA9548A
  OLED_I2C1 = OLED 128x64 I2C Monochrome Display
  OLED_I2C2 = OLED 128x64 I2C Monochrome Display
  OLED_I2C3 = OLED 128x64 I2C Monochrome Display
  ZS-042_RTC1 = ZS-042 RTC Module
  S1 = Square Pushbutton
  R3 = Resistor [tolerance=±5% resistance=100 package=THT]

nets:
  N1: Part1.D2, S1.leg0, R3.Pin_1
  GND: Part1.GND, Part2.GND
  5V: Part1.5V, Part2.VCC
  N2: Part1.A5, Part2.INPUTSCL
  N3: Part1.A4, Part2.INPUTSDA
  N4: Part2.2SDA, OLED_I2C1.SDA
  N5: Part2.2SCL, OLED_I2C1.SCK
  N6: Part2.3SDA, OLED_I2C2.SDA
  N7: Part2.3SCL, OLED_I2C2.SCK
  N8: Part2.4SDA, OLED_I2C3.SDA
  N9: Part2.4SCL, OLED_I2C3.SCK
  N10: ZS-042_RTC1.GND, R3.Pin_0

custom parts:
  Adafruit TCA9548A: You just found the perfect I2C sensor, and you want to wire up two or three or more of them to your Arduino when you realize "Uh oh, this chip has a fixed I2C address, and from what I know about I2C, you cannot have two devices with the same address on the same SDA/SCL pins!" Are you out of luck? You would be, if you didn't have this ultra-cool TCA9548A 1-to-8 I2C multiplexer! Finally, a way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

// code stored in the sketch: 3-OledClock.ino
#include <SPI.h>
#include <Wire.h>
#include <Adafruit_SSD1306.h>
#include <Time.h>
#include <DS1307RTC.h>
Adafruit_SSD1306 display(128, 64, &Wire, 4);
const int buttonPinDate = 2;
int buttonStateDate = 0;

void TCA9548A(uint8_t bus)
{
  Wire.beginTransmission(0x70);
  Wire.write(1 << bus);
  Wire.endTransmission();
}

void setup() {

  TCA9548A(2);
  display.begin(SSD1306_SWITCHCAPVCC, 0x3C);
  display.clearDisplay(); 
  
  TCA9548A(3);
  display.begin(SSD1306_SWITCHCAPVCC, 0x3C);
  display.clearDisplay();

  TCA9548A(4);
  display.begin(SSD1306_SWITCHCAPVCC, 0x3C);
  display.clearDisplay();
}

void loop() {
  
    buttonStateDate = digitalRead(buttonPinDate);
  
    TCA9548A(2);
    display.setTextColor(WHITE); display.clearDisplay();
    display.setTextSize(2); display.setCursor(45,0); display.print("Hour");
    tmElements_t tm;
    if(RTC.read(tm)){
    display.setTextSize(5);
    display.setTextColor(WHITE);
    display.setCursor(40,25);
    if (tm.Hour >= 0 && tm.Hour < 10) {
    display.write('0');}
    display.print(tm.Hour);
    display.display();
    }
  
    TCA9548A(3);
    display.setTextColor(WHITE); display.clearDisplay();
    display.setTextSize(2); display.setCursor(30,0); display.print("Minute");
    if(RTC.read(tm)){
    display.setTextSize(5);
    display.setTextColor(WHITE);
    display.setCursor(40,25);
    if (tm.Minute >= 0 && tm.Minute < 10) {
    display.write('0');}
    display.print(tm.Minute);
    display.display();
    }

    TCA9548A(4);
    display.setTextColor(WHITE); display.clearDisplay();
    display.setTextSize(2); display.setCursor(30,0); display.print("Second");    
    if(RTC.read(tm)){
    display.setTextSize(5);
    display.setTextColor(WHITE);
    display.setCursor(40,25);
    if (tm.Second >= 0 && tm.Second < 10) {
    display.write('0');}
    display.print(tm.Second);
    display.display();
    }

    if (buttonStateDate == HIGH) {

    TCA9548A(2);
    display.setTextColor(WHITE); display.clearDisplay();
    display.setTextSize(2); display.setCursor(40,0); display.print("Month");
    display.setTextSize(5);
    display.setTextColor(WHITE);
    display.setCursor(40,25);
    if (tm.Month >= 0 && tm.Month < 10) {
    display.write('0');}
    display.print(tm.Month);
    display.display();

    TCA9548A(3);
    display.setTextColor(WHITE); display.clearDisplay();
    display.setTextSize(2); display.setCursor(50,0); display.print("Day");
    display.setTextSize(5);
    display.setTextColor(WHITE);
    display.setCursor(40,25);
    if (tm.Day >= 0 && tm.Day < 10) {
    display.write('0');}
    display.print(tm.Day);
    display.display();

    TCA9548A(4);
    display.setTextColor(WHITE); display.clearDisplay();
    display.setTextSize(2); display.setCursor(45,0); display.print("Year");    
    display.setTextSize(4);
    display.setTextColor(WHITE);
    display.setCursor(20,25);
    display.print(tmYearToCalendar(tm.Year));
    display.display();
    delay(3000);
          
    }

}
